// Logisim project 6.2) Bus et registres.circ as structural Verilog: 1 circuit, main circuit main
module main (
  input  [3:0] in_1,
  input  in_2,
  input  in_3,
  input  in_4,
  input  in_5,
  input  in_6,
  input  in_7,
  input  in_8
);

  wire [3:0] controlled_buffer_1_out, register_1_q, register_2_q, register_3_q;

  assign controlled_buffer_1_out = in_2 ? in_1 : 4'bz;  // Controlled_Buffer controlled_buffer_1
  assign controlled_buffer_1_out = in_4 ? register_1_q : 4'bz;  // Controlled_Buffer controlled_buffer_2
  assign controlled_buffer_1_out = in_6 ? register_2_q : 4'bz;  // Controlled_Buffer controlled_buffer_3
  assign controlled_buffer_1_out = in_8 ? register_3_q : 4'bz;  // Controlled_Buffer controlled_buffer_4
  Hex_Digit_Display hex_digit_display_1 (.value(controlled_buffer_1_out));  // open: dp
  Register #(.width(4)) register_1 (.D(controlled_buffer_1_out), .Q(register_1_q), .clk(in_3));  // open: en, clr
  Register #(.width(4)) register_2 (.D(controlled_buffer_1_out), .Q(register_2_q), .clk(in_5));  // open: en, clr
  Register #(.width(4)) register_3 (.D(controlled_buffer_1_out), .Q(register_3_q), .clk(in_7));  // open: en, clr
endmodule
